// Logisim project computer.circ as structural Verilog: 6 circuits, main circuit main
module main (
  input  [15:0] ADDR,
  input  [7:0] DATA_IN,
  input  WE_bar,
  input  CLK,
  input  [14:0] PROG_ADDR,
  input  [7:0] PROG_DATA_IN,
  input  PROG_WE_bar,
  input  PROG_CLK,
  input  PROG_EN,
  output [7:0] DATA_OUT,
  output [7:0] PROG_DATA_OUT
);

  wire FPGA_CPU_cpu_clk, FPGA_CPU_cpu_we_bar, Muxer_display_addr_15, Muxer_display_clk, Muxer_sram_clk,
       Muxer_sram_oe, Programmer_prog_clk, Programmer_prog_en, Programmer_prog_we_bar;
  wire [1:0] Muxer_display_addr_0_1;
  wire [3:0] Video_Memory_out0, Video_Memory_out1, Video_Memory_out2, Video_Memory_out3;
  wire [7:0] FPGA_CPU_cpu_data_in, Muxer_cpu_data_out, Muxer_data_out, Muxer_prog_data_out,
       Programmer_prog_data_in;
  wire [14:0] Muxer_sram_addr, Programmer_prog_addr;
  wire [15:0] FPGA_CPU_cpu_addr;

  FPGA FPGA_CPU (
    .ADDR(ADDR), .DATA_IN(DATA_IN), .CPU_DATA_OUT(Muxer_cpu_data_out), .WE_bar(WE_bar), .CLK(CLK),
    .CPU_ADDR(FPGA_CPU_cpu_addr), .CPU_DATA_IN(FPGA_CPU_cpu_data_in), .DATA_OUT(DATA_OUT),
    .CPU_WE_Bar(FPGA_CPU_cpu_we_bar), .CPU_CLK(FPGA_CPU_cpu_clk));
  OPi Programmer (
    .ADDR(PROG_ADDR), .DATA_IN(PROG_DATA_IN), .PROG_DATA_OUT(Muxer_prog_data_out), .WE_bar(PROG_WE_bar),
    .CLK(PROG_CLK), .EN(PROG_EN), .PROG_ADDR(Programmer_prog_addr), .PROG_DATA_IN(Programmer_prog_data_in),
    .DATA_OUT(PROG_DATA_OUT), .PROG_WE_bar(Programmer_prog_we_bar), .PROG_CLK(Programmer_prog_clk),
    .PROG_EN(Programmer_prog_en));
  Mux Muxer (
    .CPU_ADDR(FPGA_CPU_cpu_addr), .CPU_WE_bar(FPGA_CPU_cpu_we_bar), .PROG_WE_bar(Programmer_prog_we_bar),
    .CPU_CLK(FPGA_CPU_cpu_clk), .PROG_ADDR(Programmer_prog_addr), .CPU_DATA_IN(FPGA_CPU_cpu_data_in),
    .PROG_DATA_IN(Programmer_prog_data_in), .CPU_DATA_OUT(Muxer_cpu_data_out),
    .PROG_DATA_OUT(Muxer_prog_data_out), .PROG_CLK(Programmer_prog_clk), .PROG_EN(Programmer_prog_en),
    .Display_Addr_0_1(Muxer_display_addr_0_1), .Display_Addr_15(Muxer_display_addr_15),
    .SRAM_OE(Muxer_sram_oe), .SRAM_Addr(Muxer_sram_addr), .Data_Out(Muxer_data_out),
    .SRAM_CLK(Muxer_sram_clk), .Display_CLK(Muxer_display_clk));  // open: Data_In
  Display Video_Memory (
    .Addr_15(Muxer_display_addr_15), .Addr_0_1(Muxer_display_addr_0_1), .Data_0_3(Muxer_data_out[3:0]),
    .CLK(Muxer_display_clk), .Out0(Video_Memory_out0), .Out1(Video_Memory_out1), .Out2(Video_Memory_out2),
    .Out3(Video_Memory_out3));
  Hex_Digit_Display hex_digit_display_1 (.value(Video_Memory_out0));  // open: dp
  RAM #(.addrWidth(15), .bus("asynch")) ram_1 (
    .addr(Muxer_sram_addr), .data(Muxer_data_out), .sel(Muxer_sram_clk), .ld(Muxer_sram_oe));  // open: clr
  Hex_Digit_Display hex_digit_display_2 (.value(Video_Memory_out1));  // open: dp
  Hex_Digit_Display hex_digit_display_3 (.value(Video_Memory_out3));  // open: dp
  Hex_Digit_Display hex_digit_display_4 (.value(Video_Memory_out2));  // open: dp
endmodule

module Display (
  input  Addr_15,
  input  [1:0] Addr_0_1,
  input  [3:0] Data_0_3,
  input  CLK,
  output [3:0] Out0,
  output [3:0] Out1,
  output [3:0] Out2,
  output [3:0] Out3
);

  wire and_1_out, and_2_out, and_3_out, and_4_out, demultiplexer_1_out0, demultiplexer_1_out1,
       demultiplexer_1_out2, demultiplexer_1_out3;

  Demultiplexer #(.select(2), .enable("false")) demultiplexer_1 (
    .out0(demultiplexer_1_out0), .out1(demultiplexer_1_out1), .out2(demultiplexer_1_out2),
    .out3(demultiplexer_1_out3), .in(Addr_15), .sel(Addr_0_1));
  and and_1 (and_1_out, CLK, demultiplexer_1_out0);
  and and_2 (and_2_out, CLK, demultiplexer_1_out1);
  and and_3 (and_3_out, CLK, demultiplexer_1_out2);
  and and_4 (and_4_out, CLK, demultiplexer_1_out3);
  Register #(.width(4), .trigger("high")) register_1 (.D(Data_0_3), .en(1'b1), .Q(Out0), .clk(and_1_out), .clr(1'b0));
  Register #(.width(4), .trigger("high")) register_2 (.D(Data_0_3), .en(1'b1), .Q(Out1), .clk(and_2_out), .clr(1'b0));
  Register #(.width(4), .trigger("high")) register_3 (.D(Data_0_3), .en(1'b1), .Q(Out2), .clk(and_3_out), .clr(1'b0));
  Register #(.width(4), .trigger("high")) register_4 (.D(Data_0_3), .en(1'b1), .Q(Out3), .clk(and_4_out), .clr(1'b0));
endmodule

module Mux (
  input  [15:0] CPU_ADDR,
  input  CPU_WE_bar,
  input  PROG_WE_bar,
  input  CPU_CLK,
  input  [14:0] PROG_ADDR,
  input  [7:0] CPU_DATA_IN,
  input  [7:0] PROG_DATA_IN,
  input  [7:0] Data_In,
  input  PROG_CLK,
  input  PROG_EN,
  output [1:0] Display_Addr_0_1,
  output Display_Addr_15,
  output SRAM_OE,
  output [14:0] SRAM_Addr,
  output [7:0] Data_Out,
  output [7:0] CPU_DATA_OUT,
  output [7:0] PROG_DATA_OUT,
  output SRAM_CLK,
  output Display_CLK
);

  wire and_1_out, and_3_out, not_1_out, not_2_out;

  not not_1 (not_1_out, PROG_EN);
  and and_1 (and_1_out, CPU_WE_bar, not_1_out);
  not not_2 (not_2_out, CPU_ADDR[15]);
  and and_2 (Display_CLK, CPU_CLK, not_1_out);
  and and_3 (and_3_out, not_2_out, Display_CLK);
  Multiplexer #(.enable("false")) multiplexer_1 (.in0(and_1_out), .in1(PROG_WE_bar), .out(SRAM_OE), .sel(PROG_EN));
  Multiplexer #(.width(8), .enable("false")) multiplexer_2 (
    .in0(CPU_DATA_IN), .in1(PROG_DATA_IN), .out(Data_Out), .sel(PROG_EN));
  Demultiplexer #(.width(8), .enable("false")) demultiplexer_1 (
    .out0(CPU_DATA_OUT), .out1(PROG_DATA_OUT), .in(Data_In), .sel(PROG_EN));
  Multiplexer #(.enable("false")) multiplexer_3 (.in0(and_3_out), .in1(PROG_CLK), .out(SRAM_CLK), .sel(PROG_EN));
  Multiplexer #(.width(15), .enable("false")) multiplexer_4 (
    .in0(CPU_ADDR[14:0]), .in1(PROG_ADDR), .out({SRAM_Addr[14:2], Display_Addr_0_1}), .sel(PROG_EN));

  assign Display_Addr_15 = CPU_ADDR[15];
  assign SRAM_Addr[1:0] = Display_Addr_0_1;
endmodule

module FPGA (
  input  [15:0] ADDR,
  input  [7:0] DATA_IN,
  input  [7:0] CPU_DATA_OUT,
  input  WE_bar,
  input  CLK,
  output [15:0] CPU_ADDR,
  output [7:0] CPU_DATA_IN,
  output [7:0] DATA_OUT,
  output CPU_WE_Bar,
  output CPU_CLK
);


  assign CPU_ADDR = ADDR;
  assign CPU_CLK = CLK;
  assign CPU_DATA_IN = DATA_IN;
  assign CPU_WE_Bar = WE_bar;
  assign DATA_OUT = CPU_DATA_OUT;
endmodule

module OPi (
  input  [14:0] ADDR,
  input  [7:0] DATA_IN,
  input  [7:0] PROG_DATA_OUT,
  input  WE_bar,
  input  CLK,
  input  EN,
  output [14:0] PROG_ADDR,
  output [7:0] PROG_DATA_IN,
  output [7:0] DATA_OUT,
  output PROG_WE_bar,
  output PROG_CLK,
  output PROG_EN
);


  assign DATA_OUT = PROG_DATA_OUT;
  assign PROG_ADDR = ADDR;
  assign PROG_CLK = CLK;
  assign PROG_DATA_IN = DATA_IN;
  assign PROG_EN = EN;
  assign PROG_WE_bar = WE_bar;
endmodule

module Mux2 (
  input  [15:0] CPU_ADDR,
  input  CPU_WE_bar,
  input  PROG_WE_bar,
  input  CPU_CLK,
  input  [14:0] PROG_ADDR,
  input  PROG_CLK,
  input  PROG_EN,
  output [1:0] Display_Addr_0_1,
  output Display_Addr_15,
  output SRAM_OE,
  output [14:0] SRAM_Addr,
  output SRAM_CLK,
  output Display_CLK
);

  wire _1st_out, _2nd_out, _3rd_out, _4th_out, multiplexer_2_out, not_1_out, transistor_1_out, undriven,
       undriven_2;

  not _1st (_1st_out, PROG_EN);
  and _2nd (_2nd_out, CPU_WE_bar, _1st_out);
  not _4th (_4th_out, CPU_ADDR[15]);
  and _1st_2 (Display_CLK, CPU_CLK, _1st_out);
  and _3rd (_3rd_out, _4th_out, Display_CLK);
  Multiplexer #(.enable("false")) multiplexer_1 (.in0(_2nd_out), .in1(PROG_WE_bar), .out(SRAM_OE), .sel(PROG_EN));
  not not_1 (not_1_out, PROG_EN);
  Multiplexer #(.enable("false")) multiplexer_2 (
    .in0(_3rd_out), .in1(PROG_CLK), .out(multiplexer_2_out), .sel(PROG_EN));
  Multiplexer #(.width(15), .enable("false")) multiplexer_3 (
    .in0(CPU_ADDR[14:0]), .in1(PROG_ADDR), .out({SRAM_Addr[14:2], Display_Addr_0_1}), .sel(PROG_EN));
  Transistor #(.\type ("n"), .gate("br")) transistor_1 (.in(undriven), .out(transistor_1_out), .gate(PROG_EN));
  Transistor #(.\type ("n")) transistor_2 (.in(undriven_2), .out(transistor_1_out), .gate(not_1_out));
  not not_2 (SRAM_CLK, multiplexer_2_out);

  assign Display_Addr_15 = CPU_ADDR[15];
  assign SRAM_Addr[1:0] = Display_Addr_0_1;
endmodule
